// Logisim project CPU.circ as structural Verilog: 5 circuits, main circuit main
module main (
  output [7:0] address,
  output [7:0] r0,
  output [1:0] addrsel,
  output [7:0] r1,
  output [7:0] r2,
  output [7:0] r3,
  output [1:0] aluop,
  output [7:0] datain,
  output [7:0] dbus,
  output [7:0] dval,
  output [7:0] sbus,
  output [7:0] aluout,
  output [1:0] phase
);

  wire clock_1_out, clock_2_out, clock_3_out, clock_4_out, clock_5_out, dwrite, imload, irload, pcload,
       pcsel, RB, readwrite, register_file_1_negative, register_file_1_zero;
  wire [1:0] dregsel, regsel, sregsel;
  wire [7:0] multiplexer_3_out, pc_adder_1_pc_out, register_1_q, register_2_q, register_3_q,
       vram_1_vram_out0, vram_1_vram_out1, vram_1_vram_out2, vram_1_vram_out3, vram_1_vram_out4,
       vram_1_vram_out5, vram_1_vram_out6, vram_1_vram_out7;

  Clock clock_1 (.out(clock_1_out));
  Clock clock_2 (.out(clock_2_out));
  RAM #(.bus("separate")) ram_1 (
    .addr(address), .din(dbus), .data(datain), .str(readwrite), .clk(clock_1_out));  // open: sel, ld, clr
  VRAM vram_1 (
    .VRAM_IN(datain), .ADD_IN(address), .RW(readwrite), .D_Write(clock_2_out), .VRAM_OUT0(vram_1_vram_out0),
    .VRAM_OUT4(vram_1_vram_out4), .VRAM_OUT1(vram_1_vram_out1), .VRAM_OUT5(vram_1_vram_out5),
    .VRAM_OUT2(vram_1_vram_out2), .VRAM_OUT6(vram_1_vram_out6), .VRAM_OUT3(vram_1_vram_out3),
    .VRAM_OUT7(vram_1_vram_out7), .CLEAR(RB));
  Multiplexer #(.select(2), .width(8), .enable("false")) multiplexer_1 (
    .in0(register_3_q), .in1(register_1_q), .in2(sbus), .in3(dbus), .out(address), .sel(addrsel));
  DotMatrix #(.matrixcols(8), .matrixrows(8)) dotmatrix_1 (
    .col0(vram_1_vram_out0), .col1(vram_1_vram_out1), .col2(vram_1_vram_out2), .col3(vram_1_vram_out3),
    .col4(vram_1_vram_out4), .col5(vram_1_vram_out5), .col6(vram_1_vram_out6), .col7(vram_1_vram_out7));
  Register register_1 (.D(datain), .en(imload), .Q(register_1_q), .clk(clock_3_out));  // open: clr
  Clock clock_3 (.out(clock_3_out));
  Multiplexer #(.select(2), .width(8), .enable("false")) multiplexer_2 (
    .in0(register_1_q), .in1(sbus), .in2(datain), .in3(aluout), .out(dval), .sel(regsel));
  Button RESET (.out(RB));
  Multiplexer #(.width(8), .enable("false")) multiplexer_3 (
    .in0(register_1_q), .in1(pc_adder_1_pc_out), .out(multiplexer_3_out), .sel(pcsel));
  Decode_Logic decode_logic_1 (
    .addrsel(addrsel), .irvalue(register_2_q), .irload(irload), .imload(imload), .dwrite(dwrite),
    .dregsel(dregsel), .sregsel(sregsel), .aluop(aluop), .regsel(regsel), .phase(phase),
    .readwrite(readwrite), .pcsel(pcsel), .zero(register_file_1_zero), .negative(register_file_1_negative),
    .pcload(pcload), .RB(RB));
  Register register_2 (.D(datain), .en(irload), .Q(register_2_q), .clk(clock_4_out));  // open: clr
  Clock clock_4 (.out(clock_4_out));
  Register register_3 (.D(multiplexer_3_out), .en(pcload), .Q(register_3_q), .clk(clock_5_out), .clr(RB));
  Clock clock_5 (.out(clock_5_out));
  PC_Adder pc_adder_1 (.PC_in(register_3_q), .PC_out(pc_adder_1_pc_out));
  Register_File register_file_1 (
    .dbus(dbus), .sbus(sbus), .dregsel(dregsel), .sregsel(sregsel), .dval(dval), .dwrite(dwrite), .r0(r0),
    .r1(r1), .r2(r2), .r3(r3), .Zero(register_file_1_zero), .Negative(register_file_1_negative));
  ALU alu_1 (.A(dbus), .B(sbus), .Result(aluout), .Operation(aluop));

  // Notes on the sheet:
  //   address bus
  //   RAM
  //   datain   bus
  //   Monitor
  //   8x8
  //   Immed
  //   8-bit CPU
  //   Befehlsregister
  //   PC
  //   Register
  //   Werte
endmodule

module Register_File (
  input  dwrite,
  input  [1:0] dregsel,
  input  [7:0] dval,
  input  [1:0] sregsel,
  output [7:0] r0,
  output [7:0] dbus,
  output [7:0] r1,
  output Zero,
  output [7:0] r2,
  output [7:0] r3,
  output Negative,
  output [7:0] sbus
);

  wire clock_1_out, demultiplexer_1_out0, demultiplexer_1_out1, demultiplexer_1_out2, demultiplexer_1_out3,
       or_1_out;

  Demultiplexer #(.select(2), .enable("false")) demultiplexer_1 (
    .out0(demultiplexer_1_out0), .out1(demultiplexer_1_out1), .out2(demultiplexer_1_out2),
    .out3(demultiplexer_1_out3), .in(dwrite), .sel(dregsel));
  Clock clock_1 (.out(clock_1_out));
  Register register_1 (.D(dval), .en(demultiplexer_1_out0), .Q(r0), .clk(clock_1_out));  // open: clr
  Register register_2 (.D(dval), .en(demultiplexer_1_out1), .Q(r1), .clk(clock_1_out));  // open: clr
  Register register_3 (.D(dval), .en(demultiplexer_1_out2), .Q(r2), .clk(clock_1_out));  // open: clr
  Register register_4 (.D(dval), .en(demultiplexer_1_out3), .Q(r3), .clk(clock_1_out));  // open: clr
  Multiplexer #(.select(2), .width(8), .enable("false")) multiplexer_1 (
    .in0(r0), .in1(r1), .in2(r2), .in3(r3), .out(dbus), .sel(dregsel));
  Multiplexer #(.select(2), .width(8), .enable("false")) multiplexer_2 (
    .in0(r0), .in1(r1), .in2(r2), .in3(r3), .out(sbus), .sel(sregsel));
  or or_1 (or_1_out, dbus[0], dbus[1], dbus[2], dbus[3], dbus[4], dbus[5], dbus[6], dbus[7]);
  not not_1 (Zero, or_1_out);

  assign Negative = dbus[7];

  // Other names for the same wires on the sheet: drs[1:0] = dregsel

  // Notes on the sheet:
  //   Register File
endmodule

module PC_Adder (
  input  [7:0] PC_in,
  output [7:0] PC_out
);

  Adder adder_1 (.a(PC_in), .b(8'h1), .out(PC_out), .cin(1'b0));  // open: cout

  // Notes on the sheet:
  //   PC Adder
endmodule

module Decode_Logic (
  input  [7:0] irvalue,
  input  RB,
  input  zero,
  input  negative,
  output [1:0] phase,
  output [1:0] dregsel,
  output [1:0] sregsel,
  output [1:0] aluop,
  output irload,
  output imload,
  output pcsel,
  output readwrite,
  output pcload,
  output [1:0] regsel,
  output dwrite,
  output [1:0] addrsel
);

  wire and_1_out, and_2_out, and_3_out, and_4_out, and_5_out, clock_1_out, multiplexer_3_out,
       multiplexer_7_out, not_1_out, not_2_out, not_3_out, not_4_out, or_1_out, or_2_out;
  wire [1:0] multiplexer_1_out, multiplexer_11_out;

  not not_1 (not_1_out, zero);
  not not_2 (not_2_out, negative);
  and and_1 (and_1_out, not_1_out, not_2_out);
  Multiplexer #(.select(4), .width(2), .enable("false")) multiplexer_1 (
    .in0(2'b11), .in1(2'b11), .in2(2'b11), .in3(2'b11), .in4(2'b10), .in5(2'b00), .in6(2'b01), .in7(2'b00),
    .in8(2'b00), .in9(2'b00), .in10(2'b00), .in11(2'b00), .in12(2'b10), .in13(2'b00), .in14(2'b00),
    .in15(2'b00), .out(multiplexer_1_out), .sel(irvalue[7:4]));
  Multiplexer #(.select(2), .enable("false")) multiplexer_2 (
    .in0(1'b1), .in1(1'b0), .in2(1'b0), .in3(1'b0), .out(irload), .sel(phase));
  not not_3 (not_3_out, irvalue[6]);
  Multiplexer #(.select(2), .enable("false")) multiplexer_3 (
    .in0(zero), .in1(not_1_out), .in2(and_1_out), .in3(negative), .out(multiplexer_3_out), .sel(irvalue[5:4]));
  and and_2 (and_2_out, not_3_out, irvalue[7], multiplexer_3_out);
  and and_3 (and_3_out, irvalue[4], irvalue[5], irvalue[6], irvalue[7]);
  Multiplexer #(.select(2), .width(2), .enable("false")) multiplexer_4 (
    .in0(2'b00), .in1(2'b00), .in2(multiplexer_1_out), .in3(2'b00), .out(regsel), .sel(phase));
  or or_1 (or_1_out, and_2_out, and_3_out);
  Multiplexer #(.select(2), .enable("false")) multiplexer_5 (
    .in0(1'b1), .in1(irvalue[7]), .in2(or_1_out), .in3(1'b0), .out(pcload), .sel(phase));
  Multiplexer #(.select(2), .enable("false")) multiplexer_6 (
    .in0(1'b0), .in1(irvalue[7]), .in2(1'b0), .in3(1'b0), .out(imload), .sel(phase));
  Multiplexer #(.select(4), .enable("false")) multiplexer_7 (
    .in0(1'b1), .in1(1'b1), .in2(1'b1), .in3(1'b1), .in4(1'b1), .in5(1'b0), .in6(1'b1), .in7(1'b0),
    .in8(1'b0), .in9(1'b0), .in10(1'b0), .in11(1'b0), .in12(1'b1), .in13(1'b0), .in14(1'b1), .in15(1'b0),
    .out(multiplexer_7_out), .sel(irvalue[7:4]));
  Counter #(.width(2), .max('h3)) counter_1 (
    .Q(phase), .clk(clock_1_out), .clr(or_2_out));  // open: load, D, count, carry
  and and_4 (and_4_out, phase[1], phase[0]);
  or or_2 (or_2_out, and_4_out, RB);
  Clock clock_1 (.out(clock_1_out));
  not not_4 (not_4_out, irvalue[5]);
  Multiplexer #(.select(2), .enable("false")) multiplexer_8 (
    .in0(1'b0), .in1(1'b0), .in2(multiplexer_7_out), .in3(1'b0), .out(dwrite), .sel(phase));
  Multiplexer #(.select(2), .enable("false")) multiplexer_9 (
    .in0(1'b1), .in1(1'b1), .in2(1'b0), .in3(1'b0), .out(pcsel), .sel(phase));
  and and_5 (and_5_out, irvalue[4], not_4_out, irvalue[6]);
  Multiplexer #(.select(2), .enable("false")) multiplexer_10 (
    .in0(1'b0), .in1(1'b0), .in2(and_5_out), .in3(1'b0), .out(readwrite), .sel(phase));
  Multiplexer #(.select(4), .width(2), .enable("false")) multiplexer_11 (
    .in0(2'b00), .in1(2'b00), .in2(2'b00), .in3(2'b00), .in4(2'b10), .in5(2'b10), .in6(2'b00), .in7(2'b00),
    .in8(2'b00), .in9(2'b00), .in10(2'b00), .in11(2'b00), .in12(2'b01), .in13(2'b01), .in14(2'b00),
    .in15(2'b00), .out(multiplexer_11_out), .sel(irvalue[7:4]));
  Multiplexer #(.select(2), .width(2), .enable("false")) multiplexer_12 (
    .in0(2'b00), .in1(2'b00), .in2(multiplexer_11_out), .in3(2'b00), .out(addrsel), .sel(phase));

  assign aluop = irvalue[5:4];
  assign dregsel = irvalue[3:2];
  assign sregsel = irvalue[1:0];

  // Other names for the same wires on the sheet: irbit4 = irvalue[4]; op1op2[3:0] = irvalue[7:4];
  //   op2[1:0] = irvalue[5:4]; irbit5 = irvalue[5]; irbit6 = irvalue[6]; op1[1:0] = irvalue[7:6]; irbit7 = irvalue[7];
  //   rd[1:0] = irvalue[3:2]; rs[1:0] = irvalue[1:0]

  // Notes on the sheet:
  //   IR Load
  //   PC Load
  //   Register Select
  //   Immed Load
  //   Decode Logic
  //   Dest Reg Write
  //   Phase
  //   Counter
  //   PC Select
  //   Read/Write
  //   Address Select
endmodule

module VRAM (
  input  [7:0] VRAM_IN,
  input  [7:0] ADD_IN,
  input  RW,
  input  D_Write,
  input  CLEAR,
  output [7:0] VRAM_OUT0,
  output [7:0] VRAM_OUT4,
  output [7:0] VRAM_OUT1,
  output [7:0] VRAM_OUT5,
  output [7:0] VRAM_OUT2,
  output [7:0] VRAM_OUT6,
  output [7:0] VRAM_OUT3,
  output [7:0] VRAM_OUT7
);

  wire and_1_out, demultiplexer_2_out0, demultiplexer_2_out1, demultiplexer_2_out2, demultiplexer_2_out3,
       demultiplexer_2_out4, demultiplexer_2_out5, demultiplexer_2_out6, demultiplexer_2_out7;
  wire [7:0] demultiplexer_1_out0, demultiplexer_1_out1, demultiplexer_1_out2, demultiplexer_1_out3,
       demultiplexer_1_out4, demultiplexer_1_out5, demultiplexer_1_out6, demultiplexer_1_out7;

  and and_1 (and_1_out, ADD_IN[3], ADD_IN[4], ADD_IN[5], ADD_IN[6], ADD_IN[7]);
  Demultiplexer #(.select(3), .width(8), .disabled(0)) demultiplexer_1 (
    .out0(demultiplexer_1_out0), .out1(demultiplexer_1_out1), .out2(demultiplexer_1_out2),
    .out3(demultiplexer_1_out3), .out4(demultiplexer_1_out4), .out5(demultiplexer_1_out5),
    .out6(demultiplexer_1_out6), .out7(demultiplexer_1_out7), .in(VRAM_IN), .sel(ADD_IN[2:0]), .en(and_1_out));
  Demultiplexer #(.select(3), .disabled(0)) demultiplexer_2 (
    .out0(demultiplexer_2_out0), .out1(demultiplexer_2_out1), .out2(demultiplexer_2_out2),
    .out3(demultiplexer_2_out3), .out4(demultiplexer_2_out4), .out5(demultiplexer_2_out5),
    .out6(demultiplexer_2_out6), .out7(demultiplexer_2_out7), .in(RW), .sel(ADD_IN[2:0]), .en(and_1_out));
  Register #(.trigger("high")) register_1 (
    .D(demultiplexer_1_out0), .en(demultiplexer_2_out0), .Q(VRAM_OUT0), .clk(and_1_out), .clr(CLEAR));
  Register #(.trigger("high")) register_2 (
    .D(demultiplexer_1_out1), .en(demultiplexer_2_out1), .Q(VRAM_OUT1), .clk(and_1_out), .clr(CLEAR));
  Register #(.trigger("high")) register_3 (
    .D(demultiplexer_1_out2), .en(demultiplexer_2_out2), .Q(VRAM_OUT2), .clk(and_1_out), .clr(CLEAR));
  Register #(.trigger("high")) register_4 (
    .D(demultiplexer_1_out3), .en(demultiplexer_2_out3), .Q(VRAM_OUT3), .clk(and_1_out), .clr(CLEAR));
  Register #(.trigger("high")) register_5 (
    .D(demultiplexer_1_out4), .en(demultiplexer_2_out4), .Q(VRAM_OUT4), .clk(and_1_out), .clr(CLEAR));
  Register #(.trigger("high")) register_6 (
    .D(demultiplexer_1_out5), .en(demultiplexer_2_out5), .Q(VRAM_OUT5), .clk(and_1_out), .clr(CLEAR));
  Register #(.trigger("high")) register_7 (
    .D(demultiplexer_1_out6), .en(demultiplexer_2_out6), .Q(VRAM_OUT6), .clk(and_1_out), .clr(CLEAR));
  Register #(.trigger("high")) register_8 (
    .D(demultiplexer_1_out7), .en(demultiplexer_2_out7), .Q(VRAM_OUT7), .clk(and_1_out), .clr(CLEAR));
endmodule
